// Logisim project V202000193_VuKy_ALU.circ as structural Verilog: 16 circuits, main circuit ALU32
module LeftShift32 (
  input  [31:0] B,
  input  [4:0] Sa,
  input  Cin,
  output [31:0] C
);

  wire [31:0] multiplexer_1_out, multiplexer_3_out, multiplexer_4_out, multiplexer_6_out, shift1_1_c,
       shift2_1_c, shift4_1_c, shift8_1_c, shift16_1_c;

  Multiplexer #(.width(32), .enable("false")) multiplexer_1 (
    .in0(B), .in1(shift1_1_c), .out(multiplexer_1_out), .sel(Sa[0]));
  Multiplexer #(.width(32), .enable("false")) multiplexer_2 (
    .in0(B), .in1(shift1_1_c), .out(multiplexer_1_out), .sel(Sa[0]));
  Shift1 shift1_1 (.Cin(Cin), .B(B), .C(shift1_1_c));
  Shift2 shift2_1 (.Cin(Cin), .B(multiplexer_1_out), .C(shift2_1_c));
  Multiplexer #(.width(32), .enable("false")) multiplexer_3 (
    .in0(multiplexer_1_out), .in1(shift2_1_c), .out(multiplexer_3_out), .sel(Sa[1]));
  Shift4 shift4_1 (.Cin(Cin), .B(multiplexer_3_out), .C(shift4_1_c));
  Multiplexer #(.width(32), .enable("false")) multiplexer_4 (
    .in0(multiplexer_3_out), .in1(shift4_1_c), .out(multiplexer_4_out), .sel(Sa[2]));
  Multiplexer #(.width(32), .enable("false")) multiplexer_5 (
    .in0(multiplexer_3_out), .in1(shift4_1_c), .out(multiplexer_4_out), .sel(Sa[2]));
  Shift8 shift8_1 (.Cin(Cin), .B(multiplexer_4_out), .C(shift8_1_c));
  Multiplexer #(.width(32), .enable("false")) multiplexer_6 (
    .in0(multiplexer_4_out), .in1(shift8_1_c), .out(multiplexer_6_out), .sel(Sa[3]));
  Shift16 shift16_1 (.Cin(Cin), .B(multiplexer_6_out), .C(shift16_1_c));
  Multiplexer #(.width(32), .enable("false")) multiplexer_7 (
    .in0(multiplexer_6_out), .in1(shift16_1_c), .out(C), .sel(Sa[4]));
endmodule

module Add32 (
  input  [31:0] A,
  input  [31:0] B,
  input  Cin,
  output V,
  output [31:0] C
);

  wire add16_1_cout, add16_2_cout, add16_2_overflow;

  Add16 add16_1 (.A(A[15:0]), .B(B[15:0]), .Cin(Cin), .Cout(add16_1_cout), .S(C[15:0]));  // open: Overflow
  Add16 add16_2 (
    .A(A[31:16]), .B(B[31:16]), .Cin(add16_1_cout), .Cout(add16_2_cout), .Overflow(add16_2_overflow),
    .S(C[31:16]));
  xor xor_1 (V, add16_2_cout, add16_2_overflow);
endmodule

module ALU32 (
  input  [31:0] A,
  input  [31:0] B,
  input  [3:0] Op,
  input  [4:0] Sa,
  output V,
  output [31:0] C
);

  wire [31:0] add_1_c, compareoperation_1_c, logicoperation_1_c, shift_1_c;

  Add add_1 (.A(A), .B(B), .Op(Op), .V(V), .C(add_1_c));
  LogicOperation logicoperation_1 (.A(B), .B(A), .Op(Op), .C(logicoperation_1_c));
  Shift shift_1 (.B(B), .Sa(Sa), .Op(Op), .C(shift_1_c));
  CompareOperation compareoperation_1 (.B(B), .A(A), .Op(Op), .C(compareoperation_1_c));
  assign C = logicoperation_1_c | add_1_c | shift_1_c | compareoperation_1_c;  // OR_Gate or_1, 32 bits wide
endmodule

module Add1 (
  input  A,
  input  B,
  input  Cin,
  output S,
  output Cout
);

  wire and_1_out, and_2_out, xor_1_out;

  xor xor_1 (xor_1_out, A, B);
  and and_1 (and_1_out, xor_1_out, Cin);
  and and_2 (and_2_out, A, B);
  xor xor_2 (S, xor_1_out, Cin);
  or or_1 (Cout, and_1_out, and_2_out);
endmodule

module Add4 (
  input  [3:0] A,
  input  [3:0] B,
  input  Cin,
  output Cout,
  output Overflow,
  output [3:0] S
);

  wire add1_1_cout, add1_2_cout;

  Add1 add1_1 (.A(A[0]), .B(B[0]), .Cin(Cin), .S(S[0]), .Cout(add1_1_cout));
  Add1 add1_2 (.A(A[1]), .B(B[1]), .Cin(add1_1_cout), .S(S[1]), .Cout(add1_2_cout));
  Add1 add1_3 (.A(A[2]), .B(B[2]), .Cin(add1_2_cout), .S(S[2]), .Cout(Overflow));
  Add1 add1_4 (.A(A[3]), .B(B[3]), .Cin(Overflow), .S(S[3]), .Cout(Cout));
endmodule

module Add16 (
  input  [15:0] A,
  input  [15:0] B,
  input  Cin,
  output Cout,
  output Overflow,
  output [15:0] S
);

  wire add4_1_cout, add4_2_cout, add4_3_cout;

  Add4 add4_1 (.A(A[3:0]), .B(B[3:0]), .Cin(Cin), .Cout(add4_1_cout), .S(S[3:0]));  // open: Overflow
  Add4 add4_2 (.A(A[7:4]), .B(B[7:4]), .Cin(add4_1_cout), .Cout(add4_2_cout), .S(S[7:4]));  // open: Overflow
  Add4 add4_3 (.A(A[11:8]), .B(B[11:8]), .Cin(add4_2_cout), .Cout(add4_3_cout), .S(S[11:8]));  // open: Overflow
  Add4 add4_4 (.A(A[15:12]), .B(B[15:12]), .Cin(add4_3_cout), .Cout(Cout), .Overflow(Overflow), .S(S[15:12]));
endmodule

module LogicOperation (
  input  [31:0] A,
  input  [31:0] B,
  input  [3:0] Op,
  output [31:0] C
);

  wire and_1_out, and_2_out, or_2_out;
  wire [0:0] not_1_out;
  wire [31:0] and_3_out, nor_1_out, or_1_out, xor_1_out;

  and and_1 (and_1_out, ~Op[1], Op[2], ~Op[3]);  // AND_Gate
  and and_2 (and_2_out, Op[1], ~Op[2], Op[3]);  // AND_Gate
  assign or_1_out = A | B;  // OR_Gate or_1, 32 bits wide
  assign and_3_out = A & B;  // AND_Gate and_3, 32 bits wide
  not not_1 (not_1_out[0], Op[0]);
  assign nor_1_out = ~(A | B);  // NOR_Gate nor_1, 32 bits wide
  assign xor_1_out = A ^ B;  // XOR_Gate xor_1, 32 bits wide
  or or_2 (or_2_out, and_1_out, and_2_out);
  Multiplexer #(.select(2), .width(32)) multiplexer_1 (
    .in0(or_1_out), .in1(and_3_out), .in2(nor_1_out), .in3(xor_1_out), .out(C), .sel({Op[1], not_1_out[0]}),
    .en(or_2_out));
endmodule

module Shift1 (
  input  Cin,
  input  [31:0] B,
  output [31:0] C
);


  assign C = {B[30:0], Cin};
endmodule

module Shift2 (
  input  Cin,
  input  [31:0] B,
  output [31:0] C
);

  wire [31:0] shift1_1_c;

  Shift1 shift1_1 (.Cin(Cin), .B(B), .C(shift1_1_c));
  Shift1 shift1_2 (.Cin(Cin), .B(shift1_1_c), .C(C));
endmodule

module Shift4 (
  input  Cin,
  input  [31:0] B,
  output [31:0] C
);

  wire [31:0] shift2_1_c;

  Shift2 shift2_1 (.Cin(Cin), .B(B), .C(shift2_1_c));
  Shift2 shift2_2 (.Cin(Cin), .B(shift2_1_c), .C(C));
endmodule

module Shift8 (
  input  Cin,
  input  [31:0] B,
  output [31:0] C
);

  wire [31:0] shift4_1_c;

  Shift4 shift4_1 (.Cin(Cin), .B(B), .C(shift4_1_c));
  Shift4 shift4_2 (.Cin(Cin), .B(shift4_1_c), .C(C));
endmodule

module Shift16 (
  input  Cin,
  input  [31:0] B,
  output [31:0] C
);

  wire [31:0] shift8_1_c;

  Shift8 shift8_1 (.Cin(Cin), .B(B), .C(shift8_1_c));
  Shift8 shift8_2 (.Cin(Cin), .B(shift8_1_c), .C(C));
endmodule

module CompareOperation (
  input  [31:0] B,
  input  [31:0] A,
  input  [3:0] Op,
  output [31:0] C
);

  wire and_4_out, and_5_out, and_6_out, and_8_out, and_9_out, not_3_out, not_4_out, or_1_out;
  wire [0:0] not_2_out;
  wire [1:0] and_2_out, and_3_out, and_3_out_2, and_3_out_3, and_3_out_4, and_7_out;
  wire [7:0] and_1_out;
  wire [31:0] bit_extender_1_out, bit_extender_2_out, bit_extender_3_out, bit_extender_4_out, not_1_out,
       xor_1_out;

  assign not_1_out = ~A;  // NOT_Gate not_1, 32 bits wide
  assign xor_1_out = B ^ A;  // XOR_Gate xor_1, 32 bits wide
  assign and_1_out = xor_1_out[7:0] & xor_1_out[15:8] & xor_1_out[23:16] & xor_1_out[31:24];  // AND_Gate and_1, 8 bits wide
  assign and_2_out = and_3_out & and_3_out_2 & and_3_out_3 & and_3_out_4;  // AND_Gate and_2, 2 bits wide
  assign {and_3_out_4, and_3_out_3, and_3_out_2, and_3_out} = not_1_out[7:0] & not_1_out[15:8] & not_1_out[23:16] & not_1_out[31:24];  // AND_Gate and_3, 8 bits wide
  and and_4 (and_4_out, and_2_out[0], and_2_out[1]);
  and and_5 (and_5_out, ~Op[1], Op[2], ~Op[3]);  // AND_Gate
  and and_6 (and_6_out, Op[1], ~Op[2], Op[3]);  // AND_Gate
  assign and_7_out = and_1_out[1:0] & and_1_out[3:2] & and_1_out[5:4] & and_1_out[7:6];  // AND_Gate and_7, 2 bits wide
  and and_8 (and_8_out, ~A[31], ~and_4_out);  // AND_Gate
  not not_2 (not_2_out[0], Op[0]);
  and and_9 (and_9_out, and_7_out[0], and_7_out[1]);
  not not_3 (not_3_out, and_9_out);
  assign bit_extender_1_out = {{31{1'b0}}, not_3_out};  // Bit_Extender bit_extender_1
  assign bit_extender_2_out = {{31{1'b0}}, and_9_out};  // Bit_Extender bit_extender_2
  not not_4 (not_4_out, and_8_out);
  assign bit_extender_3_out = {{31{1'b0}}, not_4_out};  // Bit_Extender bit_extender_3
  assign bit_extender_4_out = {{31{1'b0}}, and_8_out};  // Bit_Extender bit_extender_4
  or or_1 (or_1_out, and_5_out, and_6_out);
  Multiplexer #(.select(2), .width(32)) multiplexer_1 (
    .in0(bit_extender_1_out), .in1(bit_extender_2_out), .in2(bit_extender_3_out), .in3(bit_extender_4_out),
    .out(C), .sel({Op[1], not_2_out[0]}), .en(or_1_out));
endmodule

module Shift (
  input  [31:0] B,
  input  [4:0] Sa,
  input  [3:0] Op,
  output [31:0] C
);

  wire and_1_out, and_2_out, and_3_out, or_1_out, reverseinput_1_sign;
  wire [31:0] leftshift32_1_c, multiplexer_1_out, reverseinput_1_reverseb, reverseinput_2_reverseb;

  ReverseInput reverseinput_1 (.B(B), .ReverseB(reverseinput_1_reverseb), .Sign(reverseinput_1_sign));
  and and_1 (and_1_out, reverseinput_1_sign, Op[0]);
  and and_2 (and_2_out, ~Op[1], ~Op[2], ~Op[3]);  // AND_Gate
  and and_3 (and_3_out, ~Op[1], Op[2], Op[3]);  // AND_Gate
  Multiplexer #(.width(32)) multiplexer_1 (
    .in0(B), .in1(reverseinput_1_reverseb), .out(multiplexer_1_out), .sel(Op[3]), .en(or_1_out));
  or or_1 (or_1_out, and_2_out, and_3_out);
  LeftShift32 leftshift32_1 (.B(multiplexer_1_out), .Sa(Sa), .Cin(and_1_out), .C(leftshift32_1_c));
  ReverseInput reverseinput_2 (.B(leftshift32_1_c), .ReverseB(reverseinput_2_reverseb));  // open: Sign
  Multiplexer #(.width(32), .enable("false")) multiplexer_2 (
    .in0(leftshift32_1_c), .in1(reverseinput_2_reverseb), .out(C), .sel(Op[3]));
endmodule

module Add (
  input  [31:0] A,
  input  [31:0] B,
  input  [3:0] Op,
  output V,
  output [31:0] C
);

  wire add32_1_v, and_1_out, and_2_out, or_1_out;
  wire [31:0] add32_1_c, bit_extender_1_out, bit_extender_2_out, xor_1_out;

  assign bit_extender_1_out = {{31{Op[2]}}, Op[2]};  // Bit_Extender bit_extender_1
  assign xor_1_out = B ^ bit_extender_1_out;  // XOR_Gate xor_1, 32 bits wide
  and and_1 (and_1_out, Op[1], Op[2], ~Op[3]);  // AND_Gate
  and and_2 (and_2_out, Op[1], ~Op[1], ~Op[1]);  // AND_Gate
  Add32 add32_1 (.A(A), .B(xor_1_out), .Cin(Op[2]), .V(add32_1_v), .C(add32_1_c));
  or or_1 (or_1_out, and_1_out, and_2_out);
  and and_3 (V, add32_1_v, or_1_out);
  assign bit_extender_2_out = {{31{or_1_out}}, or_1_out};  // Bit_Extender bit_extender_2
  assign C = add32_1_c & bit_extender_2_out;  // AND_Gate and_4, 32 bits wide
endmodule

module ReverseInput (
  input  [31:0] B,
  output [31:0] ReverseB,
  output Sign
);


  assign ReverseB = {B[0], B[1], B[2], B[3], B[4], B[5], B[6], B[7], B[8], B[9], B[10], B[11], B[12], B[13], B[14], B[15], B[16], B[17], B[18], B[19], B[20], B[21], B[22], B[23], B[24], B[25], B[26], B[27], B[28], B[29], B[30], B[31]};
  assign Sign = B[31];
endmodule
